# Fritzing sketch 230V Remote (saved by Fritzing 0.8.7b)
breadboards: 1

parts:
  Part1 = Arduino Nano (Rev3.0)
  S1 = Square Pushbutton
  TRRS1 = Audio Jack (TRRS) 3.5mm [part_number="LUMBERG JEITA RC-5325A" package="RC-5325A [SMD]"]
  U1 = FS1000A - 433Mhz RF Transmitter [package=THT]

nets:
  GND: Part1.GND, S1.leg1, TRRS1.SLEEVE, U1.GND
  N1: Part1.D2, U1.DATA
  N2: Part1.D3, TRRS1.TIP
  N3: Part1.D4, S1.leg0
  5V: Part1.5V, U1.VCC

custom parts:
  FS1000A - 433Mhz RF Transmitter: This is 433Mhz RF transmitter with receiver kit for Arduino ARM MCU wireless Application environment: Remote control switch, receiver module, motorcycles, automobile anti-theft products, home security products, electric doors, shutter doors, windows, remote control socket, remote control LED, remote audio remote control electric doors, garage door remote control, remote control retractable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
